# Fritzing sketch APD (saved by Fritzing 0.9.3b)
breadboards: 1

parts:
  Raspberry_Pi_1 = Raspberry Pi 3 [part_number=RPI-3-V1.2]
  LED1 = RGB LED (com. cathode, rgb) [package="5 mm [THT]"]
  DHT1 = DHT22 Humidity and Temperature Sensor
  R1 = Resistor [tolerance=±5% resistance=10k package=THT]
  S1 = Pushbutton [package="[SMD]"]
  BUTTON2 = Arcade Button (blue)
  J1 = Piezo Speaker
  R4 = Resistor [tolerance=±5% resistance=330 package=THT]
  BUTTON3 = Arcade Button (blue)
  R6 = Resistor [tolerance=±5% resistance=330 package=THT]
  R7 = Resistor [tolerance=±5% resistance=330 package=THT]
  부품2 = Adafruit TSL2591 [part_number="Adafruit #1980"]

nets:
  3V3: Raspberry_Pi_1.3v3, Raspberry_Pi_1.3V3, R4.Pin_0, R6.Pin_1, R7.Pin_1
  N1: Raspberry_Pi_1.GPIO2, 부품2.SDA
  N2: Raspberry_Pi_1.GPIO3, 부품2.SCL
  GND: Raspberry_Pi_1.GND, DHT1.GND, S1.Pin_3, S1.Pin_4, BUTTON2.no_name_yet#2, J1.pin1, BUTTON3.no_name_yet#2, 부품2.GND
  N3: Raspberry_Pi_1.GPIO17, DHT1.DATA, R1.Pin_1
  N4: Raspberry_Pi_1.GPIO27, S1.Pin_1, S1.Pin_2, R4.Pin_1
  N5: Raspberry_Pi_1.GPIO13, LED1.blue_anode
  N6: Raspberry_Pi_1.GPIO19, LED1.green_anode
  N7: Raspberry_Pi_1.GPIO26, LED1.common_cathode
  N8: Raspberry_Pi_1.GPIO24, BUTTON3.no_name_yet#1, R7.Pin_0
  N9: Raspberry_Pi_1.GPIO23, BUTTON2.no_name_yet#1, R6.Pin_0
  N10: Raspberry_Pi_1.GPIO18, J1.pin2
  5V: Raspberry_Pi_1.5V, LED1.red_anode, DHT1.VDD, R1.Pin_0, 부품2.VIN

custom parts:
  Arcade Button (blue): Adafruit Arcade Button (blue)
  Adafruit TSL2591: When the future is dazzlingly-bright, this ultra-high-range luminosity sensor will help you measure it. The TSL2591 luminosity sensor is an advanced digital light sensor, ideal for use in a wide range of light situations. Compared to low cost CdS cells, this sensor is more precise, allowing for exact lux calculations and can be configured for different gain/timing ranges to detect light ranges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
