# Fritzing sketch IDD (saved by Fritzing 0.9.3b)
breadboards: 1

parts:
  Raspberry_Pi_Zero1 = Raspberry Pi Zero
  S2 = Pushbutton [package="[SMD]"]
  R5 = Resistor [tolerance=±5% resistance=330 package=THT]
  LED1 = Gus the Green LED
  부품2 = PowerBoost 500 Charger
  U1 = LIPO-2000mAh [package=lipo-2000]
  부품3 = Adafruit LIS3DH [part_number="Adafruit #2809"]

nets:
  N1: Raspberry_Pi_Zero1.3v3, R5.Pin_0
  N2: Raspberry_Pi_Zero1.GPIO2, 부품3.SDA
  N3: Raspberry_Pi_Zero1.GPIO3, 부품3.SCL
  GND: Raspberry_Pi_Zero1.GND, Raspberry_Pi_Zero1.GPIO27, Raspberry_Pi_Zero1.GPIO15, S2.Pin_1, S2.Pin_2, S2.Pin_3, S2.Pin_4, R5.Pin_1, LED1.anode, 부품2.GND, 부품3.GND
  N4: Raspberry_Pi_Zero1.GPIO18, LED1.cathode
  5V: Raspberry_Pi_Zero1.5V, 부품2.5.0V, 부품3.VIN
  N5: 부품2.GND_BAT_IN, U1.-
  N6: 부품2.VBAT_IN, U1.+

custom parts:
  Adafruit LIS3DH: The LIS3DH is a very popular low power triple-axis accelerometer. It's low-cost, but has just about every 'extra' you'd want in an accelerometer: Three axis sensing, 10-bit precision ±2g/±4g/±8g/±16g selectable scaling Both I2C (2 possible addresses) and SPI interface options Interrupt output Multiple data rate options 1 Hz to 5Khz As low as 2uA current draw (just the chip itself, not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
